# Fritzing sketch batteryBase (saved by Fritzing 1.0.1rc)
circuit board: 2.1cm x 2.1cm
breadboards: 1

parts:
  S1 = Toggle Switch [package=THT]
  LED1 = smd LED [color="Red (633nm)" package="0805 [SMD]"]
  R1 = Resistor [tolerance=±5% power=0.25W resistance=220 package=THT]
  BATT = Battery Holders [package=battcon_12mm_pth]
  R2 = Resistor [tolerance=±5% power=0.25W resistance=220 package=THT]
  LED2 = smd LED [color="Red (633nm)" package="0805 [SMD]"]

nets:
  N1: S1.L1, S1.COM, R1.Pin_0, BATT.+, R2.Pin_0
  N2: LED1.cathode, BATT.-, LED2.cathode
  N3: LED1.anode, R1.Pin_1
  N4: R2.Pin_1, LED2.anode
